# Fritzing sketch lcd-164 (saved by Fritzing 0.9.2b)
breadboards: 1

parts:
  U4 = LCD-16X2 [package=lcd-8x2-kit]
  R3 = Trimmer Potentiometer [maximum_resistance=10kΩ package=THT]
  R4 = Resistor [tolerance=±5% resistance=220 package=THT]
  U6 = atmega168 [package=dip]
  IC1 = SOIC-14 [chip_label=74HC164 package=SO]

nets:
  VSS: U4.VSS, U4.R_W, U4.K, R3.leg1, U6.GND, IC1.7
  VDD: U4.VDD, R3.leg2, R4.Pin_0, U6.VCC
  N1: U4.VO, R3.wiper
  N2: U4.RS, IC1.10
  N3: U4.E, IC1.11
  N4: U4.DB4, IC1.3
  N5: U4.DB5, IC1.4
  N6: U4.DB6, IC1.5
  N7: U4.DB7, IC1.6
  N8: U4.A, R4.Pin_1
  N9: U6.D0_(RX), IC1.1, IC1.2
  N10: U6.D1_(TX), IC1.8
  N11: U6.D2, IC1.9
