# Fritzing sketch lcd-595 (saved by Fritzing 0.9.2b)
breadboards: 1

parts:
  U1 = LCD-16X2 [package=lcd-8x2-kit]
  U2 = 74HC595 SMD [package="SO16 [SMD]"]
  R1 = Trimmer Potentiometer [maximum_resistance=10kΩ package=THT]
  R2 = Resistor [tolerance=±5% resistance=220 package=THT]
  U3 = atmega168 [package=dip]

nets:
  GND: U1.VSS, U1.R_W, U1.K, U2.GND, U2.OE, R1.leg1, U3.GND
  VCC: U1.VDD, U2.MR, U2.VCC, R1.leg2, R2.Pin_0, U3.VCC
  N1: U1.VO, R1.wiper
  N2: U1.RS, U2.Q1
  N3: U1.E, U2.Q3
  N4: U1.DB4, U2.Q4
  N5: U1.DB5, U2.Q5
  N6: U1.DB6, U2.Q6
  N7: U1.DB7, U2.Q7
  N8: U1.A, R2.Pin_1
  N9: U2.SH_CP, U3.D1_(TX)
  N10: U2.ST_CP, U3.D2
  N11: U2.DS, U3.D0_(RX)
